# Fritzing sketch Wemos_cat_feeder (saved by Fritzing 0.9.3b)
breadboards: 1

parts:
  J1 = Basic Servo
  Part1 = Logic Level Converter
  YwRobot_Power_Supply1 = YwRobot Breadboard Power Supply [part_number=545043]
  WeMos_D1_Mini2 = WeMos D1 Mini

nets:
  GND: J1.gnd, Part1.GND, YwRobot_Power_Supply1.GND, WeMos_D1_Mini2.G
  VCC: J1.vcc, Part1.HV, YwRobot_Power_Supply1.VCC#9, WeMos_D1_Mini2.5V
  N1: J1.pulse, Part1.TX_HV
  N2: Part1.LV, YwRobot_Power_Supply1.VCC#5
  N3: Part1.TX_LV, WeMos_D1_Mini2.D2

custom parts:
  YwRobot Breadboard Power Supply: The YwRobot Breadboard Power Supply (MB-V2) has two power rails; they can be 5V or 3V3. Power to the module can be provided through the female USB socket or through the A10 (female) 2.1mm power jack.
